# Fritzing sketch circuit (saved by Fritzing 0.9.3b)

parts:
  Part1 = Arduino Nano (Rev3.0)
  2S/3S_1500-3000mAh_LiPo/Li-Ion_Batt = LiPoly Battery (1300mAh)  # not connected
  5V_Mini_Fan = Generic male header - 3 pins [form="♂ (male)" package=THT]
  Brushless_Motor = DJI 920 KV Motor
  RX_BATT/BIND = Dagu DGServo 9g header (male) [package=THT]
  RX_THRO = Dagu DGServo 9g header (male) [package=THT]
  RX_AILE = Dagu DGServo 9g header (male) [package=THT]  # not connected
  RX_ELEV = Dagu DGServo 9g header (male) [package=THT]
  RX_RUDD = Dagu DGServo 9g header (male) [package=THT]
  RX_GEAR = Dagu DGServo 9g header (male) [package=THT]
  RX_AUX1 = Dagu DGServo 9g header (male) [package=THT]
  ESC = ESC
  M2 = Dagu DGServo 9g (Top view) [part_number=RS001B]
  Front_Right_RGB_LED = ws2812b [package="smd 2812b"]
  Front_Left_RGB_LED = ws2812b [package="smd 2812b"]
  Rear_Right_RGB_LED = ws2812b [package="smd 2812b"]
  Rear_Left_RGB_LED = ws2812b [package="smd 2812b"]
  Aux_Ring_RGB_LED = Neopixel Ring 12

nets:
  GND: Part1.GND, RX_AUX1.gnd, M2.gnd, Aux_Ring_RGB_LED.GND
  N1: Part1.D4, Aux_Ring_RGB_LED.IN
  N2: Part1.D5, Rear_Right_RGB_LED.DIN
  N3: Part1.D6, Front_Right_RGB_LED.DIN
  VCC: Part1.5V, RX_AUX1.Vcc, M2.vcc, Rear_Right_RGB_LED.VDD, Rear_Left_RGB_LED.VDD, Aux_Ring_RGB_LED.VCC
  N4: Part1.A4, RX_THRO.pulse, ESC.DATA
  N5: Part1.A3, RX_GEAR.pulse
  N6: Part1.A2, RX_RUDD.pulse
  N7: Part1.A1, RX_ELEV.pulse
  VCC_2: 5V_Mini_Fan.pin1, RX_BATT/BIND.Vcc, ESC.5V
  GND_2: 5V_Mini_Fan.pin2, RX_BATT/BIND.gnd, ESC.GND
  N8: Brushless_Motor.w, ESC.W
  N9: Brushless_Motor.v, ESC.V
  N10: Brushless_Motor.u, ESC.U
  VDD: Front_Right_RGB_LED.VDD, Front_Left_RGB_LED.VDD
  N11: Front_Right_RGB_LED.DOUT, Front_Left_RGB_LED.DIN
  VSS: Front_Right_RGB_LED.VSS, Front_Left_RGB_LED.VSS
  N12: Rear_Right_RGB_LED.DOUT, Rear_Left_RGB_LED.DIN
  VSS_2: Rear_Right_RGB_LED.VSS, Rear_Left_RGB_LED.VSS

notes:
  DSM2 ORANGE RX
  AUX1
  GEAR
  RUDD
  ELEV
  AILE
  THRO
  BATT/BIND
  Front Lamps
  2 x 1-Pixel WS2812B
  Rear/Braking Lamps
  2 x 1-Pixel WS2812B
  Aux Lamps
  8-Pixel Ring WS2812B
  2000 mAh 2S 20C Li-Po Battery
  35A RC-Car ESC
  5V Linear BEC
  4500KV 2838 Sensorless Brushless Motor
  5V Mini Fan Cooler for Raspberry Pi
  Metal Gear Steering Servo for 1:12 RC-Car

custom parts:
  LiPoly Battery (1300mAh): Lithium Ion Polymer Battery (1300mAh)
  Generic male header - 3 pins: Generic male header
  DJI 920 KV Motor: DJI Brushless Outrunner 2212/920K Motor F330-550
  Neopixel Ring 12: Neopixel Ring x12
